# Fritzing sketch arduino-station-schematic-PCB (saved by Fritzing 0.9.3b)
circuit board: 9.02206cm x 9.0976cm
breadboards: 2

parts:
  Arduino_Pro_Mini = Arduino Pro Mini v13
  C1 = Ceramic Capacitor [capacitance=100nF package="100 mil [THT, multilayer]"]
  C2 = Electrolytic Capacitor [capacitance=1µF package="100 mil [THT, electrolytic]"]
  Battery_Pack = Battery
  SOLAR_PANEL = Solar Panel [package="Renogy 50 Watts 12 Volt Monocrystalline Bendable Solar Panel"]
  DHT11 = Humidity and Temperature Sensor DHT11
  RAIN_SENSOR = YL-83 Rain Sensor - Control Board
  LIGHT_FLUX_SENSOR = Adafruit TSL2591 High Dynamic Range Digital Light Sensor [part_number="Adafruit #1980"]
  UV_SENSOR = SI1145 Digital UV Index + IR + Visible Light Sensor [part_number=1777]
  TP4056_charger = TP4056 [chip_label=TP4056 package="DIP (Dual Inline) [THT]"]
  IC1 = Voltage Regulator [part_number=MCP1700 package=SOT-89]
  jack_power_output = Screw terminal - 2 pins [package=THT]
  sim800l = sim800L v2 evb
  CO2_SENSOR = MG881 CO2 Sensor
  WIND_SPEED = A3144 Hall Effect Sensor. [package="UA [THT]"]
  WIND_DIRECTION = AS5048 [package="Breakout board"]
  ATM_SENSOR = BMP180 Breakout (GY-68)
  sim_psu_booster = mini boost module
  J1 = Dagu DGServo 9g header (male) [package=THT]  # not connected
  uploader = Dagu DGServo 9g header (male) [package=THT]  # not connected
  R3 = Resistor [tolerance=±5% resistance=100 package=THT]

nets (from the schematic view):
  N1: Arduino_Pro_Mini.D0/TX, sim800l.pin_3
  N2: Arduino_Pro_Mini.D1/RX, sim800l.pin_4
  3.3V: Arduino_Pro_Mini.VCC, DHT11.Vcc, CO2_SENSOR.Pin_2, CO2_SENSOR.Pin_5
  GND: Arduino_Pro_Mini.GND, DHT11.GND, LIGHT_FLUX_SENSOR.GND, CO2_SENSOR.Pin_3, CO2_SENSOR.Pin_6, WIND_SPEED.GND, WIND_DIRECTION.GND, ATM_SENSOR.GND
  N3: Arduino_Pro_Mini.A4, UV_SENSOR.SDA, WIND_DIRECTION.CS
  N4: Arduino_Pro_Mini.A5, WIND_DIRECTION.CLK
  N5: Arduino_Pro_Mini.A2, WIND_DIRECTION.MISO
  N6: Arduino_Pro_Mini.A1, WIND_DIRECTION.MOSI
  N7: Arduino_Pro_Mini.D9_PWM, WIND_SPEED.Out
  N8: Arduino_Pro_Mini.D8, DHT11.Data, R3.Pin_1
  N9: Arduino_Pro_Mini.D7, RAIN_SENSOR.DO
  N10: Arduino_Pro_Mini.D6_PWM, CO2_SENSOR.Pin_4
  N11: C1.0, IC1.GND
  N12: C1.1, C2.+, IC1.OUT
  N13: C2.-, jack_power_output.pin1
  N14: Battery_Pack.+, TP4056_charger.pin4
  N15: SOLAR_PANEL.Connector_1, TP4056_charger.pin1
  N16: SOLAR_PANEL.Connector_2, TP4056_charger.pin2
  N17: LIGHT_FLUX_SENSOR.SCL, UV_SENSOR.SCL, ATM_SENSOR.SCL
  3.3V_2: LIGHT_FLUX_SENSOR.3.3V, UV_SENSOR.+3V3, ATM_SENSOR.VCC
  N18: TP4056_charger.pin3, IC1.IN
  N19: TP4056_charger.pin6, jack_power_output.pin2
  N20: sim800l.pin_6, sim_psu_booster.Pin_3
  N21: sim800l.pin_7, sim_psu_booster.Pin_4

notes:
  Zettabyte IoT, Aditya Bachtiar, 2023, hgh
  Power Supply and Solar Cell
  SDA / SLC Sensors
  Digital Output Sensors
  +
  OUTPUT 3.3V
  rain sensor
  3 x 18560 Battery
  6V x 500mAH

custom parts:
  Battery: Your standard 3x 18650 battery pack (11.1 Volts)
  Solar Panel: Renogy 50 Watts 12 Volt Solar Panel
  Humidity and Temperature Sensor DHT11: Digital relative humidity & temperature sensor DHT11
  YL-83 Rain Sensor - Control Board: The YL-83 is a rain sensor that has more resistance when dry and less resistance when wet. The module runs at 5V.
  Adafruit TSL2591 High Dynamic Range Digital Light Sensor: When the future is dazzlingly-bright, this ultra-high-range luminosity sensor will help you measure it. The TSL2591 luminosity sensor is an advanced digital light sensor, ideal for use in a wide range of light situations. Compared to low cost CdS cells, this sensor is more precise, allowing for exact lux calculations and can be configured for different gain/timing ranges to detect light ranges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
  SI1145 Digital UV Index + IR + Visible Light Sensor: The SI1145 is a new sensor from SiLabs with a calibrated light sensing algorithm that can calculate UV Index. It doesn't contain an actual UV sensing element, instead it approximates it based on visible & IR light from the sun. We took this outside a couple days and compared the calculated UV index with the news-reported index and found it was very accurate! It's a digital sensor that works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
  TP4056: A DIP stand-in part for whatever IC you want. With 6 pins on a 300mil dual inline package (DIP) footprint.
  Voltage Regulator: Voltage Regulator MCP1700
  sim800L v2 evb: sim800L v2 evb GSM module.
  MG881 CO2 Sensor: This is the first CO2 sensor in the Arduino market. The output voltage of the module falls as the concentration of the CO2 increases.
  A3144 Hall Effect Sensor.: Allegro A3144 hall effect switch for high temperature operation.
  AS5048: Magnetic Rotary Encoder
  BMP180 Breakout (GY-68): This is a simple breakout board for the BMP180, a high-precision, low-power barometric pressure sensor made by Bosch Sensortec. The range of measurement is from 300hPa to 1100hPa. The sensor can be supplied with voltage ranging from 1.8V to 3.6V. Operating temperature range is -40 to +85 °C. This particular breakout board (or perhaps the configuration) is produced by Shenzhen Keep Power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
  mini boost module: mini boost module.
